// Logisim project RV32I.circ as structural Verilog
module datapath (
  input  in_1,
  output [31:0] out_2
);

  wire bsel_t, clk_t, or_1_out, regwena, wbsel_t;
  wire [1:0] ssel_t;
  wire [2:0] immsel_t, lsel_t;
  wire [3:0] alusel;
  wire [7:0] bitselector_2_out, shifter_1_out;
  wire [9:0] bitselector_1_out;
  wire [31:0] addr_t, alucontrol_1_datab, dataD, immediategenerator_1_imm31_0, ins, lw_t, pc_1_outpcplus4,
       registers_1_rs1, storeWord, sw_t;

  Clock clock_1 (.out(clk_t));
  ControlLogic controllogic_1 (
    .ins(ins), .regwena(regwena), .bsel(bsel_t), .wbsel(wbsel_t), .immsel(immsel_t), .lsel(lsel_t),
    .alusel(alusel), .ssel(ssel_t));
  Registers registers_1 (
    .clk(clk_t), .rsi1(ins[19:15]), .rsi2(ins[24:20]), .rdi(ins[11:7]), .rd(dataD), .we(regwena),
    .rs1(registers_1_rs1), .rs2(sw_t));
  ImmediateGenerator immediategenerator_1 (.ins(ins), .ins_sel(immsel_t), .imm31_0(immediategenerator_1_imm31_0));
  BitSelector #(.group(10), .width(32)) bitselector_1 (.in(addr_t), .out(bitselector_1_out), .sel(2'b00));
  ALUControl alucontrol_1 (
    .rs2(sw_t), .imm31_0(immediategenerator_1_imm31_0), .bsel(bsel_t), .dataB(alucontrol_1_datab));
  LoadControl loadcontrol_1 (.A(out_2), .lw(lw_t), .lsel(lsel_t), .wbsel(wbsel_t), .D(dataD));
  StoreControl storecontrol_1 (.wbsel(wbsel_t), .ssel(ssel_t), .sw_t(sw_t), .A(out_2), .D(storeWord));
  InstructionMemory instructionmemory_1 (.addr(bitselector_1_out), .clk(clk_t), .ins_out(ins));
  PC pc_1 (.inPC(pc_1_outpcplus4), .clk(clk_t), .rst(in_1), .outPCPlus4(pc_1_outpcplus4), .outPC(addr_t));
  BitSelector #(.group(8), .width(32)) bitselector_2 (.in(out_2), .out(bitselector_2_out), .sel(2'b00));
  Shifter #(.shift("lr")) shifter_1 (.in(bitselector_2_out), .\dist (3'b010), .out(shifter_1_out));
  or or_1 (or_1_out, ssel_t[0], ssel_t[1]);
  ALU alu_1 (.dataA(registers_1_rs1), .dataB(alucontrol_1_datab), .sel(alusel), .dataD(out_2));
  RAM #(.dataWidth(32), .enables("line")) mem (
    .addr(shifter_1_out), .we(or_1_out), .clk(clk_t), .din(storeWord), .dout(lw_t));

  // Other names for the same wires on the sheet: ALU_A[31:0] = out_2; rdi[4:0] = ins[11:7]; rs1[4:0] = ins[19:15];
  //   rs2[4:0] = ins[24:20]; rst_t = in_1
endmodule

module ISplitter (
  input  [31:0] ins,
  output [6:0] opcode,
  output [4:0] rd,
  output [2:0] funct3,
  output [4:0] rs1,
  output [11:0] imm11_0
);


  assign funct3 = ins[14:12];
  assign imm11_0 = ins[31:20];
  assign opcode = ins[6:0];
  assign rd = ins[11:7];
  assign rs1 = ins[19:15];
endmodule

module SSplitter (
  input  [31:0] ins,
  output [6:0] opcode,
  output [4:0] imm4_0,
  output [2:0] funct3,
  output [4:0] rs1,
  output [4:0] rs2,
  output [6:0] imm11_5
);


  assign funct3 = ins[14:12];
  assign imm4_0 = ins[11:7];
  assign imm11_5 = ins[31:25];
  assign opcode = ins[6:0];
  assign rs1 = ins[19:15];
  assign rs2 = ins[24:20];
endmodule

module USplitter (
  input  [31:0] ins,
  output [6:0] opcode,
  output [4:0] rd,
  output [19:0] imm31_12
);


  assign imm31_12 = ins[31:12];
  assign opcode = ins[6:0];
  assign rd = ins[11:7];
endmodule

module JSplitter (
  input  [31:0] ins,
  output [6:0] opcode,
  output [4:0] rd,
  output [7:0] imm19_12,
  output imm11,
  output [9:0] imm10_1,
  output imm20
);


  assign imm10_1 = ins[30:21];
  assign imm11 = ins[20];
  assign imm19_12 = ins[19:12];
  assign imm20 = ins[31];
  assign opcode = ins[6:0];
  assign rd = ins[11:7];
endmodule

module BSplitter (
  input  [31:0] ins,
  output [6:0] opcode,
  output imm11,
  output [3:0] imm4_1,
  output [2:0] funct3,
  output [4:0] rs1,
  output [4:0] rs2,
  output [5:0] imm10_5,
  output imm12
);


  assign funct3 = ins[14:12];
  assign imm4_1 = ins[11:8];
  assign imm10_5 = ins[30:25];
  assign imm11 = ins[7];
  assign imm12 = ins[31];
  assign opcode = ins[6:0];
  assign rs1 = ins[19:15];
  assign rs2 = ins[24:20];
endmodule

module RSplitter (
  input  [31:0] ins,
  output [6:0] opcode,
  output [4:0] rd,
  output [2:0] funct3,
  output [4:0] rs1,
  output [4:0] rs2,
  output [6:0] funct7
);


  assign funct3 = ins[14:12];
  assign funct7 = ins[31:25];
  assign opcode = ins[6:0];
  assign rd = ins[11:7];
  assign rs1 = ins[19:15];
  assign rs2 = ins[24:20];
endmodule

module ImmediateGenerator (
  input  [31:0] ins,
  input  [2:0] ins_sel,
  output [31:0] imm31_0
);

  wire [3:0] bsplitter_1_imm4_1;
  wire [4:0] ssplitter_1_imm4_0;
  wire [5:0] bsplitter_1_imm10_5;
  wire [6:0] ssplitter_1_imm11_5;
  wire [7:0] jsplitter_1_imm19_12;
  wire [9:0] jsplitter_1_imm10_1;
  wire [11:0] isplitter_1_imm11_0;
  wire [12:11] bsplitter_1_imm11;
  wire [20:11] jsplitter_1_imm11;
  wire [31:0] BOut_t, IOut_t, JOut_t, SOut_t;
  wire [31:12] UOut_t;

  ISplitter isplitter_1 (.ins(ins), .imm11_0(isplitter_1_imm11_0));  // open: opcode, rd, funct3, rs1
  SSplitter ssplitter_1 (
    .ins(ins), .imm4_0(ssplitter_1_imm4_0), .imm11_5(ssplitter_1_imm11_5));  // open: opcode, funct3, rs1, rs2
  BSplitter bsplitter_1 (
    .ins(ins), .imm11(bsplitter_1_imm11[11]), .imm4_1(bsplitter_1_imm4_1), .imm10_5(bsplitter_1_imm10_5),
    .imm12(bsplitter_1_imm11[12]));  // open: opcode, funct3, rs1, rs2
  JSplitter jsplitter_1 (
    .ins(ins), .imm19_12(jsplitter_1_imm19_12), .imm11(jsplitter_1_imm11[11]), .imm10_1(jsplitter_1_imm10_1),
    .imm20(jsplitter_1_imm11[20]));  // open: opcode, rd
  USplitter usplitter_1 (.ins(ins), .imm31_12(UOut_t));  // open: opcode, rd
  assign IOut_t = {{20{isplitter_1_imm11_0[11]}}, isplitter_1_imm11_0};  // Bit_Extender bit_extender_1
  assign SOut_t = {{20{ssplitter_1_imm11_5[6]}}, {ssplitter_1_imm11_5, ssplitter_1_imm4_0}};  // Bit_Extender bit_extender_2
  assign JOut_t = {{11{jsplitter_1_imm11[20]}}, {jsplitter_1_imm11[20], jsplitter_1_imm19_12, jsplitter_1_imm11[11], jsplitter_1_imm10_1, 1'b0}};  // Bit_Extender bit_extender_3
  assign BOut_t = {{19{bsplitter_1_imm11[12]}}, {bsplitter_1_imm11, bsplitter_1_imm10_5, bsplitter_1_imm4_1, 1'b0}};  // Bit_Extender bit_extender_4
  Multiplexer #(.select(3), .width(32)) multiplexer_1 (
    .in0(IOut_t), .in1(SOut_t), .in2(BOut_t), .in3(JOut_t), .in4({UOut_t, {12{1'b0}}}), .out(imm31_0),
    .sel(ins_sel));  // open: in5, in6, in7

  // Other names for the same wires on the sheet: imm31_0_t[31:0] = imm31_0; ins_sel_t[2:0] = ins_sel;
  //   ins_t[31:0] = ins

  // Notes on the sheet:
  //   Immediate Generator
endmodule

module PC (
  input  [31:0] inPC,
  input  clk,
  input  rst,
  output [31:0] outPCPlus4,
  output [31:0] outPC
);

  Register #(.width(32)) register_1 (.D(inPC), .en(1'b1), .clk(clk), .Q(outPC), .clr(rst));
  Adder #(.width(32)) adder_1 (.a(outPC), .b(32'h1), .out(outPCPlus4));  // open: cin, cout

  // Other names for the same wires on the sheet: clk_t = clk; inPC_t[31:0] = inPC; outPC_t[31:0] = outPC;
  //   outPCPlus4_t[31:0] = outPCPlus4; rst_t = rst
endmodule

module Registers (
  input  clk,
  input  [4:0] rsi1,
  input  [4:0] rsi2,
  input  [4:0] rdi,
  input  [31:0] rd,
  input  we,
  output [31:0] rs1,
  output [31:0] rs2
);

  wire x0we_t, x1we_t, x2we_t, x3we_t, x4we_t, x5we_t, x6we_t, x7we_t, x8we_t, x9we_t, x10we_t, x11we_t,
       x12we_t, x13we_t, x14we_t, x15we_t, x16we_t, x17we_t, x18we_t, x19we_t, x20we_t, x21we_t, x22we_t,
       x23we_t, x24we_t, x25we_t, x26we_t, x27we_t, x28we_t, x29we_t, x30we_t, x31we_t;
  wire [31:0] x1q_t, x2q_t, x3q_t, x4q_t, x5q_t, x6q_t, x7q_t, x8q_t, x9q_t, x10q_t, x11q_t, x12q_t, x13q_t,
       x14q_t, x15q_t, x16q_t, x17q_t, x18q_t, x19q_t, x20q_t, x21q_t, x22q_t, x23q_t, x24_t, x24q_t, x25q_t,
       x26q_t, x27q_t, x28q_t, x29q_t, x30q_t, x31q_t;

  Demultiplexer #(.select(5)) demultiplexer_1 (
    .out0(x0we_t), .out1(x1we_t), .out2(x2we_t), .out3(x3we_t), .out4(x4we_t), .out5(x5we_t), .out6(x6we_t),
    .out7(x7we_t), .out8(x8we_t), .out9(x9we_t), .out10(x10we_t), .out11(x11we_t), .out12(x12we_t),
    .out13(x13we_t), .out14(x14we_t), .out15(x15we_t), .out16(x16we_t), .out17(x17we_t), .out18(x18we_t),
    .out19(x19we_t), .out20(x20we_t), .out21(x21we_t), .out22(x22we_t), .out23(x23we_t), .out24(x24we_t),
    .out25(x25we_t), .out26(x26we_t), .out27(x27we_t), .out28(x28we_t), .out29(x29we_t), .out30(x30we_t),
    .out31(x31we_t), .in(we), .sel(rdi));
  Register #(.width(32)) x4 (.D(rd), .en(x4we_t), .clk(clk), .Q(x4q_t));  // open: clr
  Register #(.width(32)) x8 (.D(rd), .en(x8we_t), .clk(clk), .Q(x8q_t));  // open: clr
  Register #(.width(32)) x12 (.D(rd), .en(x12we_t), .clk(clk), .Q(x12q_t));  // open: clr
  Register #(.width(32)) x16 (.D(rd), .en(x16we_t), .clk(clk), .Q(x16q_t));  // open: clr
  Register #(.width(32)) x20 (.D(rd), .en(x20we_t), .clk(clk), .Q(x20q_t));  // open: clr
  Register #(.width(32)) x24 (.D(rd), .en(x24we_t), .clk(clk), .Q(x24q_t));  // open: clr
  Register #(.width(32)) x28 (.D(rd), .en(x28we_t), .clk(clk), .Q(x28q_t));  // open: clr
  Register #(.width(32)) x1 (.D(rd), .en(x1we_t), .clk(clk), .Q(x1q_t));  // open: clr
  Register #(.width(32)) x5 (.D(rd), .en(x5we_t), .clk(clk), .Q(x5q_t));  // open: clr
  Register #(.width(32)) x9 (.D(rd), .en(x9we_t), .clk(clk), .Q(x9q_t));  // open: clr
  Register #(.width(32)) x13 (.D(rd), .en(x13we_t), .clk(clk), .Q(x13q_t));  // open: clr
  Register #(.width(32)) x17 (.D(rd), .en(x17we_t), .clk(clk), .Q(x17q_t));  // open: clr
  Register #(.width(32)) x21 (.D(rd), .en(x21we_t), .clk(clk), .Q(x21q_t));  // open: clr
  Register #(.width(32)) x25 (.D(rd), .en(x25we_t), .clk(clk), .Q(x25q_t));  // open: clr
  Register #(.width(32)) x29 (.D(rd), .en(x29we_t), .clk(clk), .Q(x29q_t));  // open: clr
  Register #(.width(32)) x2 (.D(rd), .en(x2we_t), .clk(clk), .Q(x2q_t));  // open: clr
  Register #(.width(32)) x6 (.D(rd), .en(x6we_t), .clk(clk), .Q(x6q_t));  // open: clr
  Register #(.width(32)) x10 (.D(rd), .en(x10we_t), .clk(clk), .Q(x10q_t));  // open: clr
  Register #(.width(32)) x14 (.D(rd), .en(x14we_t), .clk(clk), .Q(x14q_t));  // open: clr
  Register #(.width(32)) x18 (.D(rd), .en(x18we_t), .clk(clk), .Q(x18q_t));  // open: clr
  Register #(.width(32)) x22 (.D(rd), .en(x22we_t), .clk(clk), .Q(x22q_t));  // open: clr
  Register #(.width(32)) x26 (.D(rd), .en(x26we_t), .clk(clk), .Q(x26q_t));  // open: clr
  Register #(.width(32)) x30 (.D(rd), .en(x30we_t), .clk(clk), .Q(x30q_t));  // open: clr
  Register #(.width(32)) x3 (.D(rd), .en(x3we_t), .clk(clk), .Q(x3q_t));  // open: clr
  Register #(.width(32)) x7 (.D(rd), .en(x7we_t), .clk(clk), .Q(x7q_t));  // open: clr
  Register #(.width(32)) x11 (.D(rd), .en(x11we_t), .clk(clk), .Q(x11q_t));  // open: clr
  Register #(.width(32)) x15 (.D(rd), .en(x15we_t), .clk(clk), .Q(x15q_t));  // open: clr
  Register #(.width(32)) x19 (.D(rd), .en(x19we_t), .clk(clk), .Q(x19q_t));  // open: clr
  Register #(.width(32)) x23 (.D(rd), .en(x23we_t), .clk(clk), .Q(x23q_t));  // open: clr
  Register #(.width(32)) x27 (.D(rd), .en(x27we_t), .clk(clk), .Q(x27q_t));  // open: clr
  Register #(.width(32)) x31 (.D(rd), .en(x31we_t), .clk(clk), .Q(x31q_t));  // open: clr
  Multiplexer #(.select(5), .width(32)) multiplexer_1 (
    .in0({32{1'b0}}), .in1(x1q_t), .in2(x2q_t), .in3(x3q_t), .in4(x4q_t), .in5(x5q_t), .in6(x6q_t),
    .in7(x7q_t), .in8(x8q_t), .in9(x9q_t), .in10(x10q_t), .in11(x11q_t), .in12(x12q_t), .in13(x13q_t),
    .in14(x14q_t), .in15(x15q_t), .in16(x16q_t), .in17(x17q_t), .in18(x18q_t), .in19(x19q_t), .in20(x20q_t),
    .in21(x21q_t), .in22(x22q_t), .in23(x23q_t), .in24(x24_t), .in25(x25q_t), .in26(x26q_t), .in27(x27q_t),
    .in28(x28q_t), .in29(x29q_t), .in30(x30q_t), .in31(x31q_t), .out(rs1), .sel(rsi1));
  Multiplexer #(.select(5), .width(32)) multiplexer_2 (
    .in0({32{1'b0}}), .in1(x1q_t), .in2(x2q_t), .in3(x3q_t), .in4(x4q_t), .in5(x5q_t), .in6(x6q_t),
    .in7(x7q_t), .in8(x8q_t), .in9(x9q_t), .in10(x10q_t), .in11(x11q_t), .in12(x12q_t), .in13(x13q_t),
    .in14(x14q_t), .in15(x15q_t), .in16(x16q_t), .in17(x17q_t), .in18(x18q_t), .in19(x19q_t), .in20(x20q_t),
    .in21(x21q_t), .in22(x22q_t), .in23(x23q_t), .in24(x24_t), .in25(x25q_t), .in26(x26q_t), .in27(x27q_t),
    .in28(x28q_t), .in29(x29q_t), .in30(x30q_t), .in31(x31q_t), .out(rs2), .sel(rsi2));

  // Other names for the same wires on the sheet: clk_t = clk; rd_t[31:0] = rd; rdi_t[4:0] = rdi; rs1_t[31:0] = rs1;
  //   rs2_t[31:0] = rs2; rsi1_t[4:0] = rsi1; rsi2_t[4:0] = rsi2; we_t = we

  // Notes on the sheet:
  //   Register File
endmodule

module ALU (
  input  [31:0] dataA,
  input  [31:0] dataB,
  input  [3:0] sel,
  output [31:0] dataD
);

  wire comparator_1_lt, comparator_2_lt;
  wire [31:0] addOut, andOut, orOut, sllOut, sltOut, sltuOut, sraOut, srlOut, subOut, xorOut;

  Adder #(.width(32)) adder_1 (.a(dataA), .b(dataB), .out(addOut));  // open: cin, cout
  Subtractor #(.width(32)) subtractor_1 (.a(dataA), .b(dataB), .out(subOut));  // open: bin, bout
  Shifter #(.width(32)) shifter_1 (.in(dataA), .\dist (dataB[4:0]), .out(sllOut));
  Comparator #(.width(32)) comparator_1 (.a(dataA), .b(dataB), .lt(comparator_1_lt));  // open: gt, eq
  Comparator #(.mode("unsigned"), .width(32)) comparator_2 (
    .a(dataA), .b(dataB), .lt(comparator_2_lt));  // open: gt, eq
  assign xorOut = dataA ^ dataB;  // XOR_Gate xor_1, 32 bits wide
  Shifter #(.shift("lr"), .width(32)) shifter_2 (.in(dataA), .\dist (dataB[4:0]), .out(srlOut));
  Shifter #(.shift("ar"), .width(32)) shifter_3 (.in(dataA), .\dist (dataB[4:0]), .out(sraOut));
  assign orOut = dataA | dataB;  // OR_Gate or_1, 32 bits wide
  assign andOut = dataA & dataB;  // AND_Gate and_1, 32 bits wide
  assign sltOut = {{31{1'b0}}, comparator_1_lt};  // Bit_Extender bit_extender_1
  assign sltuOut = {{31{1'b0}}, comparator_2_lt};  // Bit_Extender bit_extender_2
  Multiplexer #(.select(4), .width(32)) multiplexer_1 (
    .in0(addOut), .in1(sllOut), .in2(sltOut), .in3(sltuOut), .in4(xorOut), .in5(srlOut), .in6(orOut),
    .in7(andOut), .in8(subOut), .in13(sraOut), .out(dataD), .sel(sel));  // open: in9, in10, in11, in12, in14, in15

  // Other names for the same wires on the sheet: dataA_t[31:0] = dataA; dataB_t[31:0] = dataB;
  //   dataBL5_t[4:0] = dataB[4:0]; dataD_t[31:0] = dataD; sel_t[3:0] = sel

  // Notes on the sheet:
  //   ALU
  //   Sel
  //   0000
  //   1000
  //   0001
  //   0010
  //   0011
  //   0100
  //   0101
  //   1101
  //   0110
  //   0111
  //   RV32I ALU Operations
  //   Operation
  //   add-Summation
  //   sub-Subtraction
  //   sll - Shift left logical
  //   slt - Set less than
  //   sltu - Set Less than unsigned
  //   xor - eXclusive OR
  //   srl - Shift Right Logical
  //   sra - Shift right arithmetic
  //   or - logical OR
  //   and - logical AND
  //   *Sel composed of bit 6 of funct7 concatenated with funct3
endmodule

module Brancher (
  input  [31:0] dataA,
  input  [31:0] dataB,
  input  brUnsigned,
  output brLt,
  output brEq
);

  wire comparator_1_lt, comparator_2_lt;

  Comparator #(.width(32)) comparator_1 (.a(dataA), .b(dataB), .eq(brEq), .lt(comparator_1_lt));  // open: gt
  Comparator #(.mode("unsigned"), .width(32)) comparator_2 (
    .a(dataA), .b(dataB), .lt(comparator_2_lt));  // open: gt, eq
  Multiplexer multiplexer_1 (.in0(comparator_1_lt), .in1(comparator_2_lt), .out(brLt), .sel(brUnsigned));

  // Other names for the same wires on the sheet: brEq_t = brEq; brLt_t = brLt; brUn_t = brUnsigned;
  //   dataA_t[31:0] = dataA; dataB_t[31:0] = dataB
endmodule

module ControlLogic (
  input  [31:0] ins,
  output regwena,
  output bsel,
  output wbsel,
  output [2:0] immsel,
  output [2:0] lsel,
  output [3:0] alusel,
  output [1:0] ssel
);

  ROM #(.addrWidth(9), .dataWidth(15)) rom_1 (
    .addr({ins[30], ins[14:12], ins[6:2]}), .data({ssel, lsel, wbsel, alusel, regwena, immsel, bsel}));

  // Other names for the same wires on the sheet: i2_t = ins[2]; i3_t = ins[3]; i4_t = ins[4]; i5_t = ins[5];
  //   i6_t = ins[6]; i12_t = ins[12]; i13_t = ins[13]; i14_t = ins[14]; i30_t = ins[30]; bsel_t = bsel;
  //   regwena_t = regwena; wbsel_t = wbsel; as0_t = alusel[0]; as1_t = alusel[1]; as2_t = alusel[2];
  //   as3_t = alusel[3]; is0_t = immsel[0]; is1_t = immsel[1]; is2_t = immsel[2]; isel0_t = lsel[0];
  //   isel1_t = lsel[1]; isel2_t = lsel[2]; ssel0_t = ssel[0]; ssel1_t = ssel[1]

  // Notes on the sheet:
  //   contents of rom_1 (hex, n*v repeats v):
  //   11 0 0 0 211 0 0 0 2003 0 0 0 210 19*0 411 0 0 0 231 0 0 0 4003 0 0 0 230 19*0 811 0 0 0 251 0 0 0
  //   6003 0 0 0 250 23*0 271 7*0 270 19*0 1011 0 0 0 291 7*0 290 19*0 1411 0 0 0 2b1 7*0 2b0 23*0 2d1 7*0
  //   2d0 23*0 2f1 7*0 2f0 19*0 11 0 0 0 211 0 0 0 2003 0 0 0 310 19*0 411 7*0 4003 23*0 811 0 0 0 251 0 0
  //   0 6003 27*0 271 27*0 1011 0 0 0 291 27*0 1411 0 0 0 3b1 7*0 3b0 23*0 2d1 31*0 2f1
endmodule

module ALUControl (
  input  [31:0] rs2,
  input  [31:0] imm31_0,
  input  bsel,
  output [31:0] dataB
);

  Multiplexer #(.width(32)) multiplexer_1 (.in0(rs2), .in1(imm31_0), .out(dataB), .sel(bsel));
endmodule

module LoadByte (
  input  [31:0] A,
  input  [31:0] lw,
  output [31:0] lb,
  output [31:0] lbu
);

  wire [4:0] bitselector_1_out;
  wire [7:0] bitselector_2_out;
  wire [31:0] and_1_out, shifter_1_out, shifter_2_out, subtractor_1_out;

  assign and_1_out = A & 32'h3;  // AND_Gate and_1, 32 bits wide
  Subtractor #(.width(32)) subtractor_1 (.a(32'h3), .b(and_1_out), .out(subtractor_1_out));  // open: bin, bout
  Shifter #(.width(32)) shifter_1 (.in(subtractor_1_out), .\dist (5'b00011), .out(shifter_1_out));
  BitSelector #(.group(5), .width(32)) bitselector_1 (.in(shifter_1_out), .out(bitselector_1_out), .sel(3'b000));
  Shifter #(.shift("lr"), .width(32)) shifter_2 (.in(lw), .\dist (bitselector_1_out), .out(shifter_2_out));
  assign lbu = 32'hff & shifter_2_out;  // AND_Gate and_2, 32 bits wide
  BitSelector #(.group(8), .width(32)) bitselector_2 (.in(shifter_2_out), .out(bitselector_2_out), .sel(2'b00));
  assign lb = {{24{bitselector_2_out[7]}}, bitselector_2_out};  // Bit_Extender bit_extender_1

  // Other names for the same wires on the sheet: A_t[31:0] = A; lb_t[31:0] = lb; lbu_t[31:0] = lbu; lw_t[31:0] = lw
endmodule

module LoadHalfWord (
  input  [31:0] A,
  input  [31:0] lw,
  output [31:0] lh,
  output [31:0] lhu
);

  wire bitselector_1_out, not_1_out;
  wire [15:0] bitselector_2_out;

  not not_1 (not_1_out, bitselector_1_out);
  BitSelector #(.width(32)) bitselector_1 (.in(A), .out(bitselector_1_out), .sel(5'b00001));
  BitSelector #(.group(16), .width(32)) bitselector_2 (.in(lw), .out(bitselector_2_out), .sel(not_1_out));
  assign lh = {{16{bitselector_2_out[15]}}, bitselector_2_out};  // Bit_Extender bit_extender_1
  assign lhu = {{16{1'b0}}, bitselector_2_out};  // Bit_Extender bit_extender_2

  // Other names for the same wires on the sheet: A_t[31:0] = A; lh_t[31:0] = lh; lhu_t[31:0] = lhu; lw_t[31:0] = lw
endmodule

module LoadControl (
  input  [31:0] A,
  input  [31:0] lw,
  input  [2:0] lsel,
  input  wbsel,
  output [31:0] D
);

  wire [31:0] lb_t, lbu_t, lh_t, lhu_t, multiplexer_1_out;

  LoadByte loadbyte_1 (.A(A), .lw(lw), .lb(lb_t), .lbu(lbu_t));
  LoadHalfWord loadhalfword_1 (.A(A), .lw(lw), .lh(lh_t), .lhu(lhu_t));
  Multiplexer #(.select(3), .width(32)) multiplexer_1 (
    .in0(lb_t), .in1(lh_t), .in2(lw), .in4(lbu_t), .in5(lhu_t), .out(multiplexer_1_out), .sel(lsel));  // open: in3, in6, in7
  Multiplexer #(.width(32)) multiplexer_2 (.in0(multiplexer_1_out), .in1(A), .out(D), .sel(wbsel));

  // Other names for the same wires on the sheet: A_t[31:0] = A; D_t[31:0] = D; lsel_t[2:0] = lsel; lw_t[31:0] = lw;
  //   wbsel_t = wbsel
endmodule

module StoreControl (
  input  wbsel,
  input  [1:0] ssel,
  input  [31:0] sw_t,
  input  [31:0] A,
  output [31:0] D
);

  wire [31:0] multiplexer_1_out, sb_t, sh_t;

  assign sb_t = sw_t & 32'hff;  // AND_Gate and_1, 32 bits wide
  assign sh_t = sw_t & 32'hffff;  // AND_Gate and_2, 32 bits wide
  Multiplexer #(.select(2), .width(32)) multiplexer_1 (
    .in1(sb_t), .in2(sh_t), .in3(sw_t), .out(multiplexer_1_out), .sel(ssel));  // open: in0
  Multiplexer #(.width(32)) multiplexer_2 (.in0(multiplexer_1_out), .in1(A), .out(D), .sel(wbsel));

  // Other names for the same wires on the sheet: A_t[31:0] = A; D_t[31:0] = D; ssel_t[1:0] = ssel; wbsel_t = wbsel
endmodule

module StoreByte (
  input  [31:0] A,
  input  [31:0] sw,
  output [31:0] sb
);

  wire [4:0] bitselector_1_out;
  wire [31:0] and_1_out, shifter_1_out, shifter_2_out;

  assign and_1_out = A & 32'h3;  // AND_Gate and_1, 32 bits wide
  Shifter #(.width(32)) shifter_1 (.in(and_1_out), .\dist (5'b00011), .out(shifter_1_out));
  BitSelector #(.group(5), .width(32)) bitselector_1 (.in(shifter_1_out), .out(bitselector_1_out), .sel(3'b000));
  Shifter #(.shift("lr"), .width(32)) shifter_2 (.in(sw), .\dist (bitselector_1_out), .out(shifter_2_out));
  assign sb = 32'hff & shifter_2_out;  // AND_Gate and_2, 32 bits wide

  // Other names for the same wires on the sheet: A_t[31:0] = A; sb_t[31:0] = sb; sw_t[31:0] = sw
endmodule

module InstructionMemory (
  input  [9:0] addr,
  input  clk,
  output [31:0] ins_out
);

  wire [4:0] bitselector_1_out;

  ROM #(.addrWidth(5), .dataWidth(32)) rom_1 (.addr(bitselector_1_out), .data(ins_out));
  BitSelector #(.group(5), .width(10)) bitselector_1 (.in(addr), .out(bitselector_1_out), .sel(1'b0));

  // Other names for the same wires on the sheet: addr_t[9:0] = addr; clk_t = clk; ins_out_t[31:0] = ins_out

  // Notes on the sheet:
  //   contents of rom_1 (hex, n*v repeats v):
  //   3e800093 7d008113 c1810193 83018213 3e820293 0 0 0 3e820293
endmodule
